// Logisim project 8nib_RAM.circ as structural Verilog: 1 circuit, main circuit main
module main (
  input  MP,
  input  RP1,
  input  RP2,
  input  in_4,
  input  in_5,
  input  in_6,
  input  in_7,
  input  RP3,
  output out_9,
  output out_10,
  output out_11,
  output out_12
);

  wire and_1_out, and_2_out, clock_1_out, controlled_buffer_1_out, controlled_buffer_9_out,
       controlled_buffer_17_out, controlled_buffer_25_out, d_ff_1_q, d_ff_1_qn, d_ff_6_q, d_ff_7_q, d_ff_8_q,
       d_ff_9_q, d_ff_10_q, d_ff_11_q, d_ff_12_q, d_ff_13_q, d_ff_14_q, d_ff_16_q, d_ff_17_q, d_ff_18_q,
       d_ff_19_q, d_ff_20_q, d_ff_21_q, d_ff_22_q, d_ff_23_q, d_ff_24_q, d_ff_26_q, d_ff_27_q, d_ff_28_q,
       d_ff_29_q, d_ff_30_q, d_ff_31_q, d_ff_32_q, d_ff_33_q, d_ff_34_q, d_ff_36_q, d_ff_37_q, d_ff_38_q,
       d_ff_39_q, d_ff_40_q, d_ff_41_q, d_ff_42_q, d_ff_43_q, d_ff_44_q, decoder_1_out0, decoder_1_out1,
       decoder_1_out2, decoder_1_out3, decoder_1_out4, decoder_1_out5, decoder_1_out6, decoder_1_out7;
  wire [2:0] d_ff_4_q;

  D_Flip_Flop d_ff_1 (.D(MP), .clk(clock_1_out), .Q(d_ff_1_q), .Qn(d_ff_1_qn));  // open: preset, reset
  Clock clock_1 (.out(clock_1_out));
  and and_1 (and_1_out, clock_1_out, d_ff_1_qn);
  D_Flip_Flop d_ff_2 (.D(RP1), .clk(clock_1_out), .Q(d_ff_4_q[2]));  // open: Qn, preset, reset
  D_Flip_Flop d_ff_3 (.D(RP2), .clk(clock_1_out), .Q(d_ff_4_q[1]));  // open: Qn, preset, reset
  D_Flip_Flop d_ff_4 (.D(RP3), .clk(clock_1_out), .Q(d_ff_4_q[0]));  // open: Qn, preset, reset
  and and_2 (and_2_out, d_ff_1_q, clock_1_out);
  Decoder #(.select(3)) decoder_1 (
    .out0(decoder_1_out0), .out1(decoder_1_out1), .out2(decoder_1_out2), .out3(decoder_1_out3),
    .out4(decoder_1_out4), .out5(decoder_1_out5), .out6(decoder_1_out6), .out7(decoder_1_out7),
    .sel(d_ff_4_q), .en(and_1_out));
  D_Flip_Flop d_ff_5 (.D(controlled_buffer_1_out), .clk(and_2_out), .Q(out_9));  // open: Qn, preset, reset
  D_Flip_Flop d_ff_6 (.D(d_ff_14_q), .clk(decoder_1_out0), .Q(d_ff_6_q));  // open: Qn, preset, reset
  D_Flip_Flop d_ff_7 (.D(d_ff_14_q), .clk(decoder_1_out1), .Q(d_ff_7_q));  // open: Qn, preset, reset
  D_Flip_Flop d_ff_8 (.D(d_ff_14_q), .clk(decoder_1_out2), .Q(d_ff_8_q));  // open: Qn, preset, reset
  D_Flip_Flop d_ff_9 (.D(d_ff_14_q), .clk(decoder_1_out3), .Q(d_ff_9_q));  // open: Qn, preset, reset
  D_Flip_Flop d_ff_10 (.D(d_ff_14_q), .clk(decoder_1_out4), .Q(d_ff_10_q));  // open: Qn, preset, reset
  D_Flip_Flop d_ff_11 (.D(d_ff_14_q), .clk(decoder_1_out5), .Q(d_ff_11_q));  // open: Qn, preset, reset
  D_Flip_Flop d_ff_12 (.D(d_ff_14_q), .clk(decoder_1_out6), .Q(d_ff_12_q));  // open: Qn, preset, reset
  D_Flip_Flop d_ff_13 (.D(d_ff_14_q), .clk(decoder_1_out7), .Q(d_ff_13_q));  // open: Qn, preset, reset
  D_Flip_Flop d_ff_14 (.D(in_4), .clk(clock_1_out), .Q(d_ff_14_q));  // open: Qn, preset, reset
  D_Flip_Flop d_ff_15 (.D(controlled_buffer_9_out), .clk(and_2_out), .Q(out_10));  // open: Qn, preset, reset
  D_Flip_Flop d_ff_16 (.D(d_ff_24_q), .clk(decoder_1_out0), .Q(d_ff_16_q));  // open: Qn, preset, reset
  assign controlled_buffer_1_out = decoder_1_out0 ? d_ff_6_q : 1'bz;  // Controlled_Buffer controlled_buffer_1
  D_Flip_Flop d_ff_17 (.D(d_ff_24_q), .clk(decoder_1_out1), .Q(d_ff_17_q));  // open: Qn, preset, reset
  assign controlled_buffer_1_out = decoder_1_out1 ? d_ff_7_q : 1'bz;  // Controlled_Buffer controlled_buffer_2
  D_Flip_Flop d_ff_18 (.D(d_ff_24_q), .clk(decoder_1_out2), .Q(d_ff_18_q));  // open: Qn, preset, reset
  assign controlled_buffer_1_out = decoder_1_out2 ? d_ff_8_q : 1'bz;  // Controlled_Buffer controlled_buffer_3
  D_Flip_Flop d_ff_19 (.D(d_ff_24_q), .clk(decoder_1_out3), .Q(d_ff_19_q));  // open: Qn, preset, reset
  assign controlled_buffer_1_out = decoder_1_out3 ? d_ff_9_q : 1'bz;  // Controlled_Buffer controlled_buffer_4
  D_Flip_Flop d_ff_20 (.D(d_ff_24_q), .clk(decoder_1_out4), .Q(d_ff_20_q));  // open: Qn, preset, reset
  assign controlled_buffer_1_out = decoder_1_out4 ? d_ff_10_q : 1'bz;  // Controlled_Buffer controlled_buffer_5
  D_Flip_Flop d_ff_21 (.D(d_ff_24_q), .clk(decoder_1_out5), .Q(d_ff_21_q));  // open: Qn, preset, reset
  assign controlled_buffer_1_out = decoder_1_out5 ? d_ff_11_q : 1'bz;  // Controlled_Buffer controlled_buffer_6
  D_Flip_Flop d_ff_22 (.D(d_ff_24_q), .clk(decoder_1_out6), .Q(d_ff_22_q));  // open: Qn, preset, reset
  assign controlled_buffer_1_out = decoder_1_out6 ? d_ff_12_q : 1'bz;  // Controlled_Buffer controlled_buffer_7
  D_Flip_Flop d_ff_23 (.D(d_ff_24_q), .clk(decoder_1_out7), .Q(d_ff_23_q));  // open: Qn, preset, reset
  assign controlled_buffer_1_out = decoder_1_out7 ? d_ff_13_q : 1'bz;  // Controlled_Buffer controlled_buffer_8
  D_Flip_Flop d_ff_24 (.D(in_5), .clk(clock_1_out), .Q(d_ff_24_q));  // open: Qn, preset, reset
  assign controlled_buffer_9_out = decoder_1_out0 ? d_ff_16_q : 1'bz;  // Controlled_Buffer controlled_buffer_9
  assign controlled_buffer_9_out = decoder_1_out1 ? d_ff_17_q : 1'bz;  // Controlled_Buffer controlled_buffer_10
  assign controlled_buffer_9_out = decoder_1_out2 ? d_ff_18_q : 1'bz;  // Controlled_Buffer controlled_buffer_11
  assign controlled_buffer_9_out = decoder_1_out3 ? d_ff_19_q : 1'bz;  // Controlled_Buffer controlled_buffer_12
  assign controlled_buffer_9_out = decoder_1_out4 ? d_ff_20_q : 1'bz;  // Controlled_Buffer controlled_buffer_13
  assign controlled_buffer_9_out = decoder_1_out5 ? d_ff_21_q : 1'bz;  // Controlled_Buffer controlled_buffer_14
  assign controlled_buffer_9_out = decoder_1_out6 ? d_ff_22_q : 1'bz;  // Controlled_Buffer controlled_buffer_15
  assign controlled_buffer_9_out = decoder_1_out7 ? d_ff_23_q : 1'bz;  // Controlled_Buffer controlled_buffer_16
  D_Flip_Flop d_ff_25 (.D(controlled_buffer_17_out), .clk(and_2_out), .Q(out_11));  // open: Qn, preset, reset
  D_Flip_Flop d_ff_26 (.D(d_ff_34_q), .clk(decoder_1_out0), .Q(d_ff_26_q));  // open: Qn, preset, reset
  D_Flip_Flop d_ff_27 (.D(d_ff_34_q), .clk(decoder_1_out1), .Q(d_ff_27_q));  // open: Qn, preset, reset
  D_Flip_Flop d_ff_28 (.D(d_ff_34_q), .clk(decoder_1_out2), .Q(d_ff_28_q));  // open: Qn, preset, reset
  D_Flip_Flop d_ff_29 (.D(d_ff_34_q), .clk(decoder_1_out3), .Q(d_ff_29_q));  // open: Qn, preset, reset
  D_Flip_Flop d_ff_30 (.D(d_ff_34_q), .clk(decoder_1_out4), .Q(d_ff_30_q));  // open: Qn, preset, reset
  D_Flip_Flop d_ff_31 (.D(d_ff_34_q), .clk(decoder_1_out5), .Q(d_ff_31_q));  // open: Qn, preset, reset
  D_Flip_Flop d_ff_32 (.D(d_ff_34_q), .clk(decoder_1_out6), .Q(d_ff_32_q));  // open: Qn, preset, reset
  D_Flip_Flop d_ff_33 (.D(d_ff_34_q), .clk(decoder_1_out7), .Q(d_ff_33_q));  // open: Qn, preset, reset
  D_Flip_Flop d_ff_34 (.D(in_6), .clk(clock_1_out), .Q(d_ff_34_q));  // open: Qn, preset, reset
  D_Flip_Flop d_ff_35 (.D(controlled_buffer_25_out), .clk(and_2_out), .Q(out_12));  // open: Qn, preset, reset
  D_Flip_Flop d_ff_36 (.D(d_ff_44_q), .clk(decoder_1_out0), .Q(d_ff_36_q));  // open: Qn, preset, reset
  assign controlled_buffer_17_out = decoder_1_out0 ? d_ff_26_q : 1'bz;  // Controlled_Buffer controlled_buffer_17
  D_Flip_Flop d_ff_37 (.D(d_ff_44_q), .clk(decoder_1_out1), .Q(d_ff_37_q));  // open: Qn, preset, reset
  assign controlled_buffer_17_out = decoder_1_out1 ? d_ff_27_q : 1'bz;  // Controlled_Buffer controlled_buffer_18
  D_Flip_Flop d_ff_38 (.D(d_ff_44_q), .clk(decoder_1_out2), .Q(d_ff_38_q));  // open: Qn, preset, reset
  assign controlled_buffer_17_out = decoder_1_out2 ? d_ff_28_q : 1'bz;  // Controlled_Buffer controlled_buffer_19
  D_Flip_Flop d_ff_39 (.D(d_ff_44_q), .clk(decoder_1_out3), .Q(d_ff_39_q));  // open: Qn, preset, reset
  assign controlled_buffer_17_out = decoder_1_out3 ? d_ff_29_q : 1'bz;  // Controlled_Buffer controlled_buffer_20
  D_Flip_Flop d_ff_40 (.D(d_ff_44_q), .clk(decoder_1_out4), .Q(d_ff_40_q));  // open: Qn, preset, reset
  assign controlled_buffer_17_out = decoder_1_out4 ? d_ff_30_q : 1'bz;  // Controlled_Buffer controlled_buffer_21
  D_Flip_Flop d_ff_41 (.D(d_ff_44_q), .clk(decoder_1_out5), .Q(d_ff_41_q));  // open: Qn, preset, reset
  assign controlled_buffer_17_out = decoder_1_out5 ? d_ff_31_q : 1'bz;  // Controlled_Buffer controlled_buffer_22
  D_Flip_Flop d_ff_42 (.D(d_ff_44_q), .clk(decoder_1_out6), .Q(d_ff_42_q));  // open: Qn, preset, reset
  assign controlled_buffer_17_out = decoder_1_out6 ? d_ff_32_q : 1'bz;  // Controlled_Buffer controlled_buffer_23
  D_Flip_Flop d_ff_43 (.D(d_ff_44_q), .clk(decoder_1_out7), .Q(d_ff_43_q));  // open: Qn, preset, reset
  assign controlled_buffer_17_out = decoder_1_out7 ? d_ff_33_q : 1'bz;  // Controlled_Buffer controlled_buffer_24
  D_Flip_Flop d_ff_44 (.D(in_7), .clk(clock_1_out), .Q(d_ff_44_q));  // open: Qn, preset, reset
  assign controlled_buffer_25_out = decoder_1_out0 ? d_ff_36_q : 1'bz;  // Controlled_Buffer controlled_buffer_25
  assign controlled_buffer_25_out = decoder_1_out1 ? d_ff_37_q : 1'bz;  // Controlled_Buffer controlled_buffer_26
  assign controlled_buffer_25_out = decoder_1_out2 ? d_ff_38_q : 1'bz;  // Controlled_Buffer controlled_buffer_27
  assign controlled_buffer_25_out = decoder_1_out3 ? d_ff_39_q : 1'bz;  // Controlled_Buffer controlled_buffer_28
  assign controlled_buffer_25_out = decoder_1_out4 ? d_ff_40_q : 1'bz;  // Controlled_Buffer controlled_buffer_29
  assign controlled_buffer_25_out = decoder_1_out5 ? d_ff_41_q : 1'bz;  // Controlled_Buffer controlled_buffer_30
  assign controlled_buffer_25_out = decoder_1_out6 ? d_ff_42_q : 1'bz;  // Controlled_Buffer controlled_buffer_31
  assign controlled_buffer_25_out = decoder_1_out7 ? d_ff_43_q : 1'bz;  // Controlled_Buffer controlled_buffer_32
endmodule
