// Logisim project computer.circ as structural Verilog: 18 circuits, main circuit main
module main (
  input  [2:0] in_1,
  input  [3:0] in_2,
  input  [3:0] in_3,
  input  [3:0] in_4,
  input  [3:0] in_5,
  input  [3:0] in_6,
  input  [3:0] in_7,
  input  [3:0] in_8,
  input  [3:0] in_9,
  input  [3:0] in_10,
  input  [3:0] in_11
);

  wire alu_2_1_neg, alu_2_1_op, alu_2_1_over, alu_2_1_sign_over, alu_2_1_zero, ALUSrc, clock_1_out, Fetch,
       ir_1_dest0, ir_1_dest1, MemReg, MemWrite, RegWrite, SetData_out;
  wire [2:0] ALUOp, ctrl, pc_1_cur_adr, pc_1_view_address;
  wire [3:0] alu_2_1_result, alu_2_1_viewl, alu_2_1_viewr, alu_2_1_viewresult, data_ram_1_data0,
       data_ram_1_data1, data_ram_1_readdata, instruction_ram_1_cur_instruction, instruction_ram_1_i0,
       instruction_ram_1_i1, instruction_ram_1_i2, instruction_ram_1_i3, instruction_ram_1_i4,
       instruction_ram_1_i5, instruction_ram_1_i6, instruction_ram_1_i7, ir_1_opcode, ir_1_view_opcode,
       multiplexer_1_out, multiplexer_2_out, register_block_1_readdata0, register_block_1_readdata1,
       register_block_1_view0, register_block_1_view1, sign_extend_1_dout;

  // Probe on 4'b1111
  // Probe on 4'b0101
  // Probe on 4'b1101
  // Probe on 4'b0001
  // Probe on 4'b0010
  // Probe on 4'b0100
  // Probe on 4'b1000
  // Probe on 4'b0000
  // Probe on pc_1_view_address
  PC pc_1 (.Fetch(Fetch), .start(in_1), .control(ctrl), .cur_adr(pc_1_cur_adr), .view_address(pc_1_view_address));
  // Probe on instruction_ram_1_i7
  // Probe on instruction_ram_1_i6
  // Probe on instruction_ram_1_i5
  // Probe on instruction_ram_1_i4
  // Probe on instruction_ram_1_i3
  // Probe on instruction_ram_1_i2
  // Probe on instruction_ram_1_i1
  // Probe on instruction_ram_1_i0
  instruction_ram instruction_ram_1 (
    .ii1(in_10), .ii0(in_11), .ii7(in_2), .ii6(in_3), .ii5(in_4), .ii4(in_6), .ii3(in_7), .ii2(in_9),
    .control(ctrl), .address(pc_1_cur_adr), .cur_instruction(instruction_ram_1_cur_instruction),
    .i7(instruction_ram_1_i7), .i6(instruction_ram_1_i6), .i5(instruction_ram_1_i5),
    .i4(instruction_ram_1_i4), .i3(instruction_ram_1_i3), .i2(instruction_ram_1_i2),
    .i1(instruction_ram_1_i1), .i0(instruction_ram_1_i0));
  // Probe on ir_1_view_opcode
  // Probe on 4'b1111
  // Probe on 4'b0100
  // Probe on 4'b1000
  // Probe on 4'b0101
  // Probe on 4'b1101
  // Probe on 4'b1110
  // Probe on 4'b0001
  // Probe on 4'b0010
  ir ir_1 (
    .instruction(instruction_ram_1_cur_instruction), .control(ctrl), .Fetch(Fetch), .opcode(ir_1_opcode),
    .view_opcode(ir_1_view_opcode), .dest0(ir_1_dest0), .dest1(ir_1_dest1));
  control control_1 (
    .opcode(ir_1_opcode), .control(ctrl), .Fetch(Fetch), .ALUSrc(ALUSrc), .ALUOp(ALUOp), .MemtoReg(MemReg),
    .MemWrite(MemWrite), .RegWrite(RegWrite));
  // Probe on register_block_1_view0
  Clock clock_1 (.out(clock_1_out));
  reset reset_1 (.activate(SetData_out), .clock(clock_1_out), .control(ctrl));
  // Probe on register_block_1_view1
  // Probe on nothing
  Button SetData (.out(SetData_out));
  register_block register_block_1 (
    .ReadReg0(ir_1_dest0), .ReadReg1(ir_1_dest1), .RegWrite(RegWrite), .WriteData(multiplexer_2_out),
    .control(ctrl), .View0(register_block_1_view0), .View1(register_block_1_view1),
    .ReadData0(register_block_1_readdata0), .ReadData1(register_block_1_readdata1));
  sign_extend sign_extend_1 (.din(ir_1_dest0), .dout(sign_extend_1_dout));
  Multiplexer #(.width(4)) multiplexer_1 (
    .in0(register_block_1_readdata1), .in1(sign_extend_1_dout), .out(multiplexer_1_out), .sel(ALUSrc));
  // Probe on alu_2_1_viewl
  // Probe on alu_2_1_neg
  // Probe on 4'b1111
  // Probe on 4'b0101
  // Probe on 4'b1101
  // Probe on 4'b0110
  // Probe on 4'b1110
  // Probe on 4'b0001
  // Probe on 4'b1011
  // Probe on 4'b0010
  // Probe on alu_2_1_op
  // Probe on alu_2_1_viewr
  // Probe on alu_2_1_viewresult
  // Probe on alu_2_1_zero
  // Probe on alu_2_1_over
  ALU_2 alu_2_1 (
    .R_in(multiplexer_1_out), .L_in(register_block_1_readdata0), .ALUOp(ALUOp), .control(ctrl),
    .viewResult(alu_2_1_viewresult), .result(alu_2_1_result), .op(alu_2_1_op), .viewL(alu_2_1_viewl),
    .viewR(alu_2_1_viewr), .neg(alu_2_1_neg), .zero(alu_2_1_zero), .sign_over(alu_2_1_sign_over),
    .over(alu_2_1_over));
  // Probe on alu_2_1_sign_over
  // Probe on data_ram_1_data0
  // Probe on data_ram_1_data1
  data_ram data_ram_1 (
    .ii0(in_5), .ii1(in_8), .control(ctrl), .MemWrite(MemWrite), .WriteData(register_block_1_readdata1),
    .Address(alu_2_1_result), .Data0(data_ram_1_data0), .Data1(data_ram_1_data1),
    .ReadData(data_ram_1_readdata));
  Multiplexer #(.width(4)) multiplexer_2 (
    .in0(alu_2_1_result), .in1(data_ram_1_readdata), .out(multiplexer_2_out), .sel(MemReg));

  // Notes on the sheet:
  //   Test 1:
  //   Noah Tonnesen
  //   260948469
  //   (s0 + s0) = 2s0 -> s0
  //   s1 - 2s0 = 2s0 - s1 -> s1
  //   instruction 7  --  halt
  //   instruction 6  --  save r0->s1
  //   instruction 5  --  sub r0-r1->r0
  //   instruction 4  --  load s1->r0
  //   instruction 3  --  load s0->r1
  //   instruction 2  --  save r0->s0
  //   instruction 1  --  add r0+r0->r0
  //   instruction 0  --  load s0->r0
  //   Test 1.1:     Start:  s0=-1  s1=3     End:  s0=-2  s1=5
  //   Test 1.2:     Start:  s0=2  s1=7      End:  s0=4  s1=3
  //   Test 1.3:     Start:  s0=-2  s1=-2     End:  s0=-4  s1=2
  //   For the grader:
  //   3. Turn on the clock to run instructions
  //   4. Watch component outputs ('view' field)
  //   Test 2:
  //   (2s1 - s0) - (2s1 - s0) =0 -> s0
  //   s1 - (s0 - s1) = 2s1 - s0 -> s1
  //   1. Enter data into Instruction RAM, Data RAM, and Program Counter ('set' field)
  //   2. Click the 'SetData' button below to clear all flip flops and fill with the entered data
  //   You will see the updates in the 'view' field. Make sure the clock is off.
  //   instruction 7  --  halt
  //   instruction 6  --  save r0->s0
  //   instruction 5  --  sub r0-r0->r0
  //   instruction 4  --  save r0->s1
  //   instruction 3  --  sub r0-r1->r0
  //   instruction 2  --  sub r1-r0->r1
  //   instruction 1  --  load s1-> r0
  //   instruction 0  --  load s0->r1
  //   Test 2.1:     Start:  s0=0  s1=3     End:  s0=-6  s1=-3
  //   Test 2.2:     Start:  s0=4  s1=-3      End:  s0=6  s1=3
  //   Test 2.3:     Start:  s0=-2  s1=-2     End:  s0=4  s1=2
  //   Test 3:
  //   instruction 7  --  halt
  //   (s0 + s0) - s1 = 2s0 - s1 -> s0
  //   s1 - (2s0 - s1) = 2s1 - 2s0-> s1
  //   instruction 6  --  save r0->s1
  //   instruction 5  --  sub r0-r1->r0
  //   instruction 4  --  save r1->s0
  //   instruction 3  --  sub r1-r0->r1
  //   instruction 2  --  load s1->r0
  //   instruction 1  --  add r1+r1->r1
  //   instruction 0  --  load s0->r1
  //   Test 3.1:     Start:  s0=0  s1=3     End:  s0=-3  s1=6
  //   Test 3.2:     Start:  s0=1  s1=-1      End:  s0=3  s1=-4
  //   Test 3.3:     Start:  s0=-2  s1=-4     End:  s0=0  s1=-4
endmodule

module PC (
  input  Fetch,
  input  [2:0] start,
  input  [2:0] control,
  output [2:0] cur_adr,
  output [2:0] view_address
);

  wire and_4_out, and_5_out, d_ff_2_q, not_1_out, s0, s1, s2;
  wire [2:0] xor_3_out;

  and and_1 (s0, start[0], control[1]);
  and and_2 (s1, start[1], control[1]);
  D_Flip_Flop d_ff_1 (.D(xor_3_out[2]), .clk(d_ff_2_q), .Q(cur_adr[2]), .preset(s2), .reset(control[0]));  // open: Qn
  and and_3 (s2, start[2], control[1]);
  D_Flip_Flop #(.trigger("falling")) d_ff_2 (
    .clk(control[2]), .D(Fetch), .Q(d_ff_2_q), .reset(not_1_out));  // open: Qn, preset
  not not_1 (not_1_out, Fetch);
  D_Flip_Flop d_ff_3 (.D(xor_3_out[1]), .clk(d_ff_2_q), .Q(cur_adr[1]), .preset(s1), .reset(control[0]));  // open: Qn
  xor xor_1 (xor_3_out[2], cur_adr[2], and_4_out);
  xor xor_2 (xor_3_out[1], cur_adr[1], and_5_out);
  xor xor_3 (xor_3_out[0], cur_adr[0], 1'b1);
  D_Flip_Flop d_ff_4 (.D(xor_3_out[0]), .clk(d_ff_2_q), .Q(cur_adr[0]), .preset(s0), .reset(control[0]));  // open: Qn
  and and_4 (and_4_out, and_5_out, cur_adr[1]);
  and and_5 (and_5_out, cur_adr[0], 1'b1);

  assign view_address = cur_adr;
endmodule

module ir (
  input  [3:0] instruction,
  input  [2:0] control,
  input  Fetch,
  output [3:0] opcode,
  output [3:0] view_opcode,
  output dest0,
  output dest1
);

  D_Flip_Flop d_ff_1 (.D(instruction[3]), .clk(Fetch), .Q(opcode[3]), .reset(control[0]));  // open: Qn, preset
  D_Flip_Flop d_ff_2 (.D(instruction[2]), .clk(Fetch), .Q(opcode[2]), .reset(control[0]));  // open: Qn, preset
  D_Flip_Flop d_ff_3 (.D(instruction[1]), .clk(Fetch), .Q(dest1), .reset(control[0]));  // open: Qn, preset
  D_Flip_Flop d_ff_4 (.D(instruction[0]), .clk(Fetch), .Q(dest0), .reset(control[0]));  // open: Qn, preset

  assign opcode[1:0] = {dest1, dest0};
  assign view_opcode = {opcode[3:2], dest1, dest0};
endmodule

module instruction_ram (
  input  [3:0] ii7,
  input  [3:0] ii6,
  input  [3:0] ii5,
  input  [3:0] ii4,
  input  [3:0] ii3,
  input  [3:0] ii2,
  input  [3:0] ii1,
  input  [3:0] ii0,
  input  [2:0] address,
  input  [2:0] control,
  output [3:0] i7,
  output [3:0] i6,
  output [3:0] i5,
  output [3:0] i4,
  output [3:0] i3,
  output [3:0] i2,
  output [3:0] i1,
  output [3:0] i0,
  output [3:0] cur_instruction
);

  wire [3:0] controlled_buffer_1_dout, controlled_buffer_2_dout, controlled_buffer_3_dout,
       controlled_buffer_4_dout, controlled_buffer_5_dout, controlled_buffer_6_dout,
       controlled_buffer_7_dout, controlled_buffer_8_dout;

  controlled_buffer controlled_buffer_1 (.din(ii7), .thru(control[1]), .dout(controlled_buffer_1_dout));
  controlled_buffer controlled_buffer_2 (.din(ii6), .thru(control[1]), .dout(controlled_buffer_2_dout));
  controlled_buffer controlled_buffer_3 (.din(ii5), .thru(control[1]), .dout(controlled_buffer_3_dout));
  controlled_buffer controlled_buffer_4 (.din(ii4), .thru(control[1]), .dout(controlled_buffer_4_dout));
  controlled_buffer controlled_buffer_5 (.din(ii3), .thru(control[1]), .dout(controlled_buffer_5_dout));
  controlled_buffer controlled_buffer_6 (.din(ii2), .thru(control[1]), .dout(controlled_buffer_6_dout));
  controlled_buffer controlled_buffer_7 (.din(ii1), .thru(control[1]), .dout(controlled_buffer_7_dout));
  controlled_buffer controlled_buffer_8 (.din(ii0), .thru(control[1]), .dout(controlled_buffer_8_dout));
  instruction_nibble instruction_nibble_1 (.clear(control[0]), .set_data(controlled_buffer_1_dout), .cur_data(i7));
  instruction_nibble instruction_nibble_2 (.clear(control[0]), .set_data(controlled_buffer_2_dout), .cur_data(i6));
  instruction_nibble instruction_nibble_3 (.clear(control[0]), .set_data(controlled_buffer_3_dout), .cur_data(i5));
  instruction_nibble instruction_nibble_4 (.clear(control[0]), .set_data(controlled_buffer_4_dout), .cur_data(i4));
  instruction_nibble instruction_nibble_5 (.clear(control[0]), .set_data(controlled_buffer_5_dout), .cur_data(i3));
  instruction_nibble instruction_nibble_6 (.clear(control[0]), .set_data(controlled_buffer_6_dout), .cur_data(i2));
  instruction_nibble instruction_nibble_7 (.clear(control[0]), .set_data(controlled_buffer_7_dout), .cur_data(i1));
  instruction_nibble instruction_nibble_8 (.clear(control[0]), .set_data(controlled_buffer_8_dout), .cur_data(i0));
  Multiplexer #(.select(3), .width(4)) multiplexer_1 (
    .in0(i0), .in1(i1), .in2(i2), .in3(i3), .in4(i4), .in5(i5), .in6(i6), .in7(i7), .out(cur_instruction),
    .sel(address));
endmodule

module control (
  input  [2:0] control,
  input  [3:0] opcode,
  output Fetch,
  output ALUSrc,
  output [2:0] ALUOp,
  output MemtoReg,
  output MemWrite,
  output RegWrite
);

  wire and_1_out, and_5_out, d_ff_2_q, d_ff_3_q, decoder_1_out1, halt, or_1_out, or_3_out, reset;

  and and_1 (and_1_out, ~halt, control[2]);  // AND_Gate
  Decoder decoder_1 (.out0(ALUOp[1]), .out1(decoder_1_out1), .sel(opcode[3]), .en(Fetch));
  D_Flip_Flop #(.trigger("high")) d_ff_1 (.Q(Fetch), .preset(and_1_out), .reset(reset));  // open: clk, D, Qn
  and and_2 (halt, opcode[0], opcode[1], opcode[2], opcode[3]);
  or or_1 (or_1_out, ALUOp[1], decoder_1_out1);
  and and_3 (ALUOp[0], decoder_1_out1, opcode[2]);
  D_Flip_Flop #(.trigger("falling")) d_ff_2 (
    .clk(control[2]), .D(ALUOp[1]), .Q(d_ff_2_q), .reset(reset));  // open: Qn, preset
  Decoder decoder_2 (.out0(MemtoReg), .out1(MemWrite), .sel(opcode[2]), .en(d_ff_2_q));
  and and_4 (ALUOp[2], or_1_out, control[2]);
  D_Flip_Flop #(.trigger("falling")) d_ff_3 (
    .clk(control[2]), .D(decoder_1_out1), .Q(d_ff_3_q), .reset(reset));  // open: Qn, preset
  or or_2 (RegWrite, MemtoReg, d_ff_3_q);
  or or_3 (or_3_out, RegWrite, MemWrite);
  and and_5 (and_5_out, or_3_out, control[2]);
  or or_4 (reset, and_5_out, control[0]);

  assign ALUSrc = ALUOp[1];

  // Other names for the same wires on the sheet: Sub = ALUOp[0]; CalcALU = ALUOp[2]; clr = control[0];
  //   clk = control[2]; op0 = opcode[2]; op1 = opcode[3]
endmodule

module register_block (
  input  ReadReg0,
  input  ReadReg1,
  input  RegWrite,
  input  [3:0] WriteData,
  input  [2:0] control,
  output [3:0] View0,
  output [3:0] ReadData0,
  output [3:0] ReadData1,
  output [3:0] View1
);

  wire decoder_1_out0, decoder_1_out1;

  Decoder decoder_1 (.out0(decoder_1_out0), .out1(decoder_1_out1), .sel(ReadReg1), .en(RegWrite));
  nibble nibble_1 (
    .write(decoder_1_out0), .clear(control[0]), .data_in(WriteData), .cur_data(View0));  // open: set_data
  nibble nibble_2 (
    .write(decoder_1_out1), .clear(control[0]), .data_in(WriteData), .cur_data(View1));  // open: set_data
  Multiplexer #(.width(4)) multiplexer_1 (.in0(View0), .in1(View1), .out(ReadData0), .sel(ReadReg0));
  Multiplexer #(.width(4)) multiplexer_2 (.in0(View0), .in1(View1), .out(ReadData1), .sel(ReadReg1));

  // Other names for the same wires on the sheet: read0 = ReadReg0; read1 = ReadReg1
endmodule

module data_ram (
  input  MemWrite,
  input  [3:0] WriteData,
  input  [3:0] Address,
  input  [3:0] ii0,
  input  [3:0] ii1,
  input  [2:0] control,
  output [3:0] ReadData,
  output [3:0] Data0,
  output [3:0] Data1
);

  wire w0, w1;
  wire [3:0] controlled_buffer_1_dout, controlled_buffer_2_dout;

  controlled_buffer controlled_buffer_1 (.din(ii0), .thru(control[1]), .dout(controlled_buffer_1_dout));
  controlled_buffer controlled_buffer_2 (.din(ii1), .thru(control[1]), .dout(controlled_buffer_2_dout));
  Decoder decoder_1 (.out0(w0), .out1(w1), .sel(Address[0]), .en(MemWrite));
  nibble nibble_1 (
    .write(w0), .clear(control[0]), .data_in(WriteData), .set_data(controlled_buffer_1_dout), .cur_data(Data0));
  Multiplexer #(.width(4)) multiplexer_1 (.in0(Data0), .in1(Data1), .out(ReadData), .sel(Address[0]));
  nibble nibble_2 (
    .write(w1), .clear(control[0]), .data_in(WriteData), .set_data(controlled_buffer_2_dout), .cur_data(Data1));

  // Other names for the same wires on the sheet: clr = control[0]; data[3:0] = WriteData
endmodule

module alu (
  input  [3:0] L_in,
  input  [3:0] R_in,
  input  [3:0] ALUOp,
  input  [2:0] control,
  output [3:0] viewL,
  output [3:0] viewR,
  output [3:0] result,
  output neg,
  output over,
  output zero,
  output sign_over,
  output [3:0] view,
  output op
);

  wire and_1_out, and_2_out, and_3_out, and_4_out, and_5_out, and_6_out, and_7_out, and_8_out, and_9_out,
       and_10_out, and_11_out, and_12_out, and_13_out, and_14_out, and_15_out, and_16_out, and_17_out,
       and_18_out, and_19_out, C1, C2, C3, C4, d_ff_17_qn, O1, O2, O3, O4, or_1_out, or_3_out, or_5_out,
       or_7_out, or_9_out, or_10_out, or_11_out, R1, R2, R3, R4, xor_1_out, xor_3_out, xor_5_out, xor_7_out;
  wire [3:0] multiplexer_1_out;

  D_Flip_Flop d_ff_1 (.D(L_in[3]), .clk(ALUOp[0]), .Q(viewL[3]), .reset(control[0]));  // open: Qn, preset
  Multiplexer #(.width(4)) multiplexer_1 (.in0(R_in), .in1(4'b0000), .out(multiplexer_1_out), .sel(ALUOp[2]));
  D_Flip_Flop d_ff_2 (.D(multiplexer_1_out[3]), .clk(ALUOp[0]), .Q(viewR[3]), .reset(control[0]));  // open: Qn, preset
  and and_1 (and_1_out, viewL[3], R4);
  and and_2 (and_2_out, viewL[3], C3);
  or or_1 (or_1_out, and_1_out, and_2_out);
  or or_2 (C4, or_1_out, and_3_out);
  xor xor_1 (xor_1_out, viewL[3], R4);
  D_Flip_Flop d_ff_3 (.D(L_in[2]), .clk(ALUOp[0]), .Q(viewL[2]), .reset(control[0]));  // open: Qn, preset
  D_Flip_Flop d_ff_4 (.D(multiplexer_1_out[2]), .clk(ALUOp[0]), .Q(viewR[2]), .reset(control[0]));  // open: Qn, preset
  and and_3 (and_3_out, R4, C3);
  and and_4 (and_4_out, viewL[2], R3);
  or or_3 (or_3_out, and_4_out, and_5_out);
  xor xor_2 (O4, xor_1_out, C3);
  D_Flip_Flop d_ff_5 (.D(O4), .clk(ALUOp[3]), .Q(result[3]), .reset(control[0]));  // open: Qn, preset
  // Probe on result
  D_Flip_Flop d_ff_6 (.D(L_in[1]), .clk(ALUOp[0]), .Q(viewL[1]), .reset(control[0]));  // open: Qn, preset
  D_Flip_Flop d_ff_7 (.D(multiplexer_1_out[1]), .clk(ALUOp[0]), .Q(viewR[1]), .reset(control[0]));  // open: Qn, preset
  and and_5 (and_5_out, viewL[2], C2);
  and and_6 (and_6_out, R3, C2);
  or or_4 (C3, or_3_out, and_6_out);
  xor xor_3 (xor_3_out, viewL[2], R3);
  xor xor_4 (O3, xor_3_out, C2);
  D_Flip_Flop d_ff_8 (.D(O3), .clk(ALUOp[3]), .Q(result[2]), .reset(control[0]));  // open: Qn, preset
  D_Flip_Flop d_ff_9 (.D(L_in[0]), .clk(ALUOp[0]), .Q(viewL[0]), .reset(control[0]));  // open: Qn, preset
  D_Flip_Flop d_ff_10 (.D(multiplexer_1_out[0]), .clk(ALUOp[0]), .Q(viewR[0]), .reset(control[0]));  // open: Qn, preset
  and and_7 (and_7_out, viewL[1], R2);
  and and_8 (and_8_out, viewL[1], C1);
  or or_5 (or_5_out, and_7_out, and_8_out);
  or or_6 (C2, or_5_out, and_9_out);
  D_Flip_Flop d_ff_11 (.D(O2), .clk(ALUOp[3]), .Q(result[1]), .reset(control[0]));  // open: Qn, preset
  and and_9 (and_9_out, R2, C1);
  and and_10 (and_10_out, viewL[0], R1);
  xor xor_5 (xor_5_out, viewL[1], R2);
  xor xor_6 (O2, xor_5_out, C1);
  D_Flip_Flop d_ff_12 (.D(O1), .clk(ALUOp[3]), .Q(result[0]), .reset(control[0]));  // open: Qn, preset
  and and_11 (and_11_out, viewL[0], ALUOp[1]);
  and and_12 (and_12_out, R1, ALUOp[1]);
  or or_7 (or_7_out, and_10_out, and_11_out);
  or or_8 (C1, or_7_out, and_12_out);
  xor xor_7 (xor_7_out, viewL[0], R1);
  xor xor_8 (O1, xor_7_out, ALUOp[1]);
  xor xor_9 (R4, ALUOp[1], viewR[3]);
  xor xor_10 (R3, ALUOp[1], viewR[2]);
  and and_13 (and_13_out, viewL[3], R4, O4);
  and and_14 (and_14_out, and_13_out, ~C4);  // AND_Gate
  D_Flip_Flop d_ff_13 (.D(O4), .clk(ALUOp[3]), .Q(neg), .reset(or_11_out));  // open: Qn, preset
  xor xor_11 (R1, ALUOp[1], viewR[0]);
  xor xor_12 (R2, ALUOp[1], viewR[1]);
  and and_15 (and_15_out, ~R4, ~ALUOp[1], C4);  // AND_Gate
  and and_16 (and_16_out, O4, ~viewL[3], ~R4);  // AND_Gate
  or or_9 (or_9_out, and_14_out, and_16_out, and_15_out);
  D_Flip_Flop d_ff_14 (.D(or_9_out), .clk(ALUOp[3]), .Q(over), .reset(or_11_out));  // open: Qn, preset
  and and_17 (and_17_out, ~O4, ~O3, ~O2, ~O1);  // AND_Gate
  D_Flip_Flop d_ff_15 (.D(and_17_out), .clk(ALUOp[3]), .Q(zero), .reset(or_11_out));  // open: Qn, preset
  and and_18 (and_18_out, ~C4, C3);  // AND_Gate
  and and_19 (and_19_out, C4, ~C3);  // AND_Gate
  or or_10 (or_10_out, and_18_out, and_19_out);
  D_Flip_Flop d_ff_16 (.D(or_10_out), .clk(ALUOp[3]), .Q(sign_over), .reset(or_11_out));  // open: Qn, preset
  D_Flip_Flop d_ff_17 (.Qn(d_ff_17_qn), .preset(ALUOp[3]), .reset(control[0]));  // open: clk, D, Q
  or or_11 (or_11_out, d_ff_17_qn, ~ALUOp[0]);  // OR_Gate

  assign op = ALUOp[1];
  assign view = result;

  // Other names for the same wires on the sheet: load = ALUOp[0]; thru = ALUOp[2]; calc = ALUOp[3]; clr = control[0];
  //   L1 = viewL[0]; L2 = viewL[1]; L3 = viewL[2]; L4 = viewL[3]; r1_t = viewR[0]; r2_t = viewR[1]; r3_t = viewR[2];
  //   r4_t = viewR[3]

  // Notes on the sheet:
  //   carry out
  //   4 carry
  //   4 out
  //   3 carry
  //   3 out
  //   2 carry
  //   2 out
  //   1 carry
  //   1 out
  //   input
  //   carry in
  //   complement
  //   status
endmodule

module nibble (
  input  write,
  input  clear,
  input  [3:0] data_in,
  input  [3:0] set_data,
  output [3:0] cur_data
);

  D_Flip_Flop d_ff_1 (.clk(write), .D(data_in[3]), .Q(cur_data[3]), .preset(set_data[3]), .reset(clear));  // open: Qn
  D_Flip_Flop d_ff_2 (.clk(write), .D(data_in[2]), .Q(cur_data[2]), .preset(set_data[2]), .reset(clear));  // open: Qn
  D_Flip_Flop d_ff_3 (.clk(write), .D(data_in[1]), .Q(cur_data[1]), .preset(set_data[1]), .reset(clear));  // open: Qn
  D_Flip_Flop d_ff_4 (.clk(write), .D(data_in[0]), .Q(cur_data[0]), .preset(set_data[0]), .reset(clear));  // open: Qn
endmodule

module instruction_nibble (
  input  clear,
  input  [3:0] set_data,
  output [3:0] cur_data
);

  D_Flip_Flop d_ff_1 (.Q(cur_data[3]), .preset(set_data[3]), .reset(clear));  // open: clk, D, Qn
  D_Flip_Flop d_ff_2 (.Q(cur_data[2]), .preset(set_data[2]), .reset(clear));  // open: clk, D, Qn
  D_Flip_Flop d_ff_3 (.Q(cur_data[1]), .preset(set_data[1]), .reset(clear));  // open: clk, D, Qn
  D_Flip_Flop d_ff_4 (.Q(cur_data[0]), .preset(set_data[0]), .reset(clear));  // open: clk, D, Qn
endmodule

module controlled_buffer (
  input  thru,
  input  [3:0] din,
  output [3:0] dout
);

  and and_1 (dout[0], din[0], thru);
  and and_2 (dout[1], din[1], thru);
  and and_3 (dout[2], din[2], thru);
  and and_4 (dout[3], din[3], thru);
endmodule

module reset (
  input  activate,
  input  clock,
  output [2:0] control
);

  D_Flip_Flop #(.trigger("falling")) d_ff_1 (
    .clk(activate), .D(1'b1), .Q(control[1]), .reset(clock));  // open: Qn, preset

  assign {control[2], control[0]} = {clock, activate};
endmodule

module sign_extend (
  input  din,
  output [3:0] dout
);


  assign dout = {3'b000, din};

  // Notes on the sheet:
  //   sign extend
endmodule

module op_adder (
  input  L_in,
  input  R_in,
  input  carry_in,
  output carry_out,
  output result
);

  wire and_1_out, and_2_out, and_3_out, or_1_out, xor_1_out;

  and and_1 (and_1_out, L_in, R_in);
  and and_2 (and_2_out, L_in, carry_in);
  or or_1 (or_1_out, and_1_out, and_2_out);
  or or_2 (carry_out, or_1_out, and_3_out);
  and and_3 (and_3_out, R_in, carry_in);
  xor xor_1 (xor_1_out, L_in, R_in);
  xor xor_2 (result, xor_1_out, carry_in);

  // Other names for the same wires on the sheet: CIn = carry_in; COut = carry_out; L = L_in; O = result; R = R_in

  // Notes on the sheet:
  //   carry out
  //   carry in
  //   result
endmodule

module ALU_2 (
  input  [3:0] R_in,
  input  [3:0] L_in,
  input  [2:0] ALUOp,
  input  [2:0] control,
  output [3:0] viewL,
  output [3:0] viewResult,
  output [3:0] result,
  output [3:0] viewR,
  output op,
  output neg,
  output zero,
  output sign_over,
  output over
);

  wire op_adder_1_carry_out, op_adder_2_carry_out;
  wire [3:0] alu_res_nibble_2_cur_data, complement_1_bits_out, result_t;
  wire [3:2] op_adder_3_carry_out;

  alu_res_nibble alu_res_nibble_1 (.write(ALUOp[2]), .clear(control[0]), .data_in(R_in), .cur_data(viewL));
  alu_res_nibble alu_res_nibble_2 (
    .write(ALUOp[2]), .clear(control[0]), .data_in(L_in), .cur_data(alu_res_nibble_2_cur_data));
  Multiplexer #(.width(4)) multiplexer_1 (.in0(alu_res_nibble_2_cur_data), .in1(4'b0000), .out(viewR), .sel(ALUOp[1]));
  complement complement_1 (.activate(ALUOp[0]), .bits_in(viewR), .bits_out(complement_1_bits_out));
  op_adder op_adder_1 (
    .L_in(viewL[0]), .R_in(complement_1_bits_out[0]), .carry_in(ALUOp[0]), .carry_out(op_adder_1_carry_out),
    .result(result_t[0]));
  op_adder op_adder_2 (
    .L_in(viewL[1]), .R_in(complement_1_bits_out[1]), .carry_in(op_adder_1_carry_out),
    .carry_out(op_adder_2_carry_out), .result(result_t[1]));
  op_adder op_adder_3 (
    .L_in(viewL[2]), .R_in(complement_1_bits_out[2]), .carry_in(op_adder_2_carry_out),
    .carry_out(op_adder_3_carry_out[2]), .result(result_t[2]));
  op_adder op_adder_4 (
    .L_in(viewL[3]), .R_in(complement_1_bits_out[3]), .carry_in(op_adder_3_carry_out[2]),
    .carry_out(op_adder_3_carry_out[3]), .result(result_t[3]));
  alu_status alu_status_1 (
    .result(result_t), .adder_bits({op_adder_3_carry_out, complement_1_bits_out[3], viewL[3]}),
    .control({ALUOp[0], ALUOp[2], control[0]}), .over(over), .zero(zero), .neg(neg), .sign_over(sign_over));
  alu_res_nibble alu_res_nibble_3 (.write(ALUOp[2]), .clear(control[0]), .data_in(result_t), .cur_data(result));

  assign op = ALUOp[0];
  assign viewResult = result;

  // Other names for the same wires on the sheet: clr = control[0]; calc = ALUOp[2]; thru = ALUOp[1]; clk = control[2]
endmodule

module complement (
  input  [3:0] bits_in,
  input  activate,
  output [3:0] bits_out
);

  xor xor_1 (bits_out[3], activate, bits_in[3]);
  xor xor_2 (bits_out[2], activate, bits_in[2]);
  xor xor_3 (bits_out[1], activate, bits_in[1]);
  xor xor_4 (bits_out[0], activate, bits_in[0]);
endmodule

module alu_status (
  input  [3:0] adder_bits,
  input  [2:0] control,
  input  [3:0] result,
  output neg,
  output zero,
  output sign_over,
  output over
);

  wire and_1_out, and_2_out, and_3_out, and_4_out, and_5_out, and_6_out, and_7_out, and_8_out, or_1_out,
       or_2_out;

  and and_1 (and_1_out, ~adder_bits[3], adder_bits[2]);  // AND_Gate
  and and_2 (and_2_out, adder_bits[3], ~adder_bits[2]);  // AND_Gate
  or or_1 (or_1_out, and_1_out, and_2_out);
  D_Flip_Flop #(.trigger("high")) d_ff_1 (
    .D(or_1_out), .clk(control[1]), .Q(sign_over), .reset(control[0]));  // open: Qn, preset
  and and_3 (and_3_out, adder_bits[0], adder_bits[1], ~adder_bits[3], result[3]);  // AND_Gate
  and and_4 (and_4_out, result[3], ~adder_bits[0], ~adder_bits[1]);  // AND_Gate
  or or_2 (or_2_out, and_3_out, and_4_out, and_5_out);
  and and_5 (and_5_out, ~adder_bits[1], ~control[2], adder_bits[3]);  // AND_Gate
  and and_6 (and_6_out, or_2_out, ~and_7_out);  // AND_Gate
  D_Flip_Flop #(.trigger("high")) d_ff_2 (
    .D(and_6_out), .clk(control[1]), .Q(over), .reset(control[0]));  // open: Qn, preset
  and and_7 (and_7_out, ~result[3], ~result[2], ~result[1], ~result[0]);  // AND_Gate
  and and_8 (and_8_out, result[3], ~or_1_out);  // AND_Gate
  D_Flip_Flop #(.trigger("high")) d_ff_3 (
    .D(and_7_out), .clk(control[1]), .Q(zero), .reset(control[0]));  // open: Qn, preset
  D_Flip_Flop #(.trigger("high")) d_ff_4 (
    .clk(control[1]), .D(and_8_out), .Q(neg), .reset(control[0]));  // open: Qn, preset

  // Other names for the same wires on the sheet: clr = control[0]; calc = control[1]
endmodule

module alu_res_nibble (
  input  write,
  input  clear,
  input  [3:0] data_in,
  output [3:0] cur_data
);

  D_Flip_Flop #(.trigger("high")) d_ff_1 (
    .clk(write), .D(data_in[3]), .Q(cur_data[3]), .reset(clear));  // open: Qn, preset
  D_Flip_Flop #(.trigger("high")) d_ff_2 (
    .clk(write), .D(data_in[2]), .Q(cur_data[2]), .reset(clear));  // open: Qn, preset
  D_Flip_Flop #(.trigger("high")) d_ff_3 (
    .clk(write), .D(data_in[1]), .Q(cur_data[1]), .reset(clear));  // open: Qn, preset
  D_Flip_Flop #(.trigger("high")) d_ff_4 (
    .clk(write), .D(data_in[0]), .Q(cur_data[0]), .reset(clear));  // open: Qn, preset
endmodule
