// Logisim project mini6.circ as structural Verilog: 1 circuit, main circuit main
module main (
  input  in_1,
  input  in_2,
  input  R_input,
  input  in_4,
  input  in_5,
  input  in_6,
  input  in_7,
  input  in_8,
  input  in_9,
  input  in_10,
  input  in_11,
  input  in_12,
  input  in_13,
  input  in_14,
  input  in_15,
  input  in_16,
  input  in_17,
  input  in_18,
  input  in_19,
  input  in_20,
  input  in_21,
  input  in_22,
  input  in_23,
  input  in_24,
  output out_25,
  output out_26,
  output out_27,
  output out_28,
  output out_29,
  output out_30,
  output out_31,
  output out_32,
  output out_33,
  output out_34,
  output out_35,
  output out_36,
  output out_37,
  output out_38,
  output out_39,
  output out_40,
  output out_41
);

  wire and_1_out, and_2_out, and_4_out, and_5_out, and_6_out, and_7_out, and_8_out, and_9_out, and_10_out,
       and_11_out, and_12_out, and_13_out, and_14_out, and_15_out, and_16_out, and_17_out, and_18_out,
       and_19_out, and_20_out, and_23_out, and_24_out, and_25_out, c0, c1, c2, clk, d_ff_9_q, d_ff_12_q,
       d_ff_13_q, d_ff_14_q, i1, i2, i3, l0, L1, l1_t, L2, l2_t, L3, l3_t, not_1_out, not_2_out, not_3_out,
       not_4_out, not_5_out, not_6_out, not_7_out, or_2_out, or_5_out, or_8_out, r0, R1, r1_t, R2, r2_t, R3,
       r3_t, xor_2_out, xor_4_out, xor_5_out, xor_6_out;

  D_Flip_Flop d_ff_1 (.D(in_15), .clk(clk), .Q(L3));  // open: Qn, preset, reset
  xor xor_1 (out_40, L1, R1);
  D_Flip_Flop d_ff_2 (.D(in_16), .clk(clk), .Q(L2));  // open: Qn, preset, reset
  and and_1 (and_1_out, L1, R1);
  xor xor_2 (xor_2_out, L2, R2);
  xor xor_3 (out_39, and_1_out, xor_2_out);
  D_Flip_Flop d_ff_3 (.D(in_8), .clk(clk), .Q(R3));  // open: Qn, preset, reset
  D_Flip_Flop d_ff_4 (.D(in_17), .clk(clk), .Q(L1));  // open: Qn, preset, reset
  and and_2 (and_2_out, L2, R2);
  xor xor_4 (xor_4_out, L3, R3);
  xor xor_5 (xor_5_out, out_39, and_2_out);
  nor nor_1 (out_38, xor_5_out, xor_4_out);
  and and_3 (out_37, ~out_38, xor_4_out);  // AND_Gate
  D_Flip_Flop d_ff_5 (.D(in_9), .clk(clk), .Q(R2));  // open: Qn, preset, reset
  and and_4 (and_4_out, L3, R3);
  D_Flip_Flop d_ff_6 (.D(in_10), .clk(clk), .Q(R1));  // open: Qn, preset, reset
  and and_5 (and_5_out, r3_t, c2);
  and and_6 (and_6_out, l3_t, c2);
  and and_7 (and_7_out, r3_t, l3_t);
  or or_1 (out_29, and_5_out, and_6_out, and_7_out);
  and and_8 (and_8_out, ~out_29, or_2_out);  // AND_Gate
  and and_9 (and_9_out, r2_t, c1);
  or or_2 (or_2_out, r3_t, l3_t, c2);
  and and_10 (and_10_out, r3_t, l3_t, c2);
  or or_3 (out_25, and_8_out, and_10_out);
  and and_11 (and_11_out, l2_t, c1);
  and and_12 (and_12_out, r2_t, l2_t);
  or or_4 (c2, and_9_out, and_11_out, and_12_out);
  and and_13 (and_13_out, ~c2, or_5_out);  // AND_Gate
  not not_1 (not_1_out, i3);
  and and_14 (and_14_out, r1_t, c0);
  or or_5 (or_5_out, r2_t, l2_t, c1);
  and and_15 (and_15_out, r2_t, l2_t, c1);
  or or_6 (out_26, and_13_out, and_15_out);
  not not_2 (not_2_out, i2);
  and and_16 (and_16_out, l1_t, c0);
  and and_17 (and_17_out, r1_t, l1_t);
  or or_7 (c1, and_14_out, and_16_out, and_17_out);
  and and_18 (and_18_out, ~c1, or_8_out);  // AND_Gate
  not not_3 (not_3_out, i1);
  or or_8 (or_8_out, r1_t, l1_t, c0);
  and and_19 (and_19_out, r1_t, l1_t, c0);
  or or_9 (out_27, and_18_out, and_19_out);
  and and_20 (and_20_out, r0, l0);
  xor xor_6 (xor_6_out, r0, l0);
  and and_21 (out_28, ~and_20_out, xor_6_out);  // AND_Gate
  or or_10 (c0, and_20_out, in_1);
  not not_4 (not_4_out, in_18);
  // AND_Gate and_22 has open pins: in0=and_23_out, in1=out_33, out=open
  xor xor_7 (out_33, and_23_out, not_4_out);
  not not_5 (not_5_out, in_19);
  and and_23 (and_23_out, and_24_out, ~out_34);  // AND_Gate
  xor xor_8 (out_34, and_24_out, not_5_out);
  and and_24 (and_24_out, and_25_out, ~out_35);  // AND_Gate
  Clock clock_1 (.out(clk));
  D_Flip_Flop d_ff_7 (.D(in_4), .clk(clk), .Q(l3_t));  // open: Qn, preset, reset
  not not_6 (not_6_out, in_20);
  xor xor_9 (out_35, and_25_out, not_6_out);
  and and_25 (and_25_out, in_1, ~out_36);  // AND_Gate
  not not_7 (not_7_out, in_21);
  xor xor_10 (out_36, in_1, not_7_out);
  D_Flip_Flop d_ff_8 (.D(in_5), .clk(clk), .Q(l2_t));  // open: Qn, preset, reset
  D_Flip_Flop d_ff_9 (.D(in_11), .clk(clk), .Q(d_ff_9_q));  // open: Qn, preset, reset
  D_Flip_Flop d_ff_10 (.D(in_6), .clk(clk), .Q(l1_t));  // open: Qn, preset, reset
  xor xor_11 (r3_t, d_ff_9_q, in_1);
  D_Flip_Flop d_ff_11 (.D(in_7), .clk(clk), .Q(l0));  // open: Qn, preset, reset
  D_Flip_Flop d_ff_12 (.D(in_12), .clk(clk), .Q(d_ff_12_q));  // open: Qn, preset, reset
  xor xor_12 (r2_t, d_ff_12_q, in_1);
  D_Flip_Flop d_ff_13 (.D(in_13), .clk(clk), .Q(d_ff_13_q));  // open: Qn, preset, reset
  D_Flip_Flop d_ff_14 (.D(in_14), .clk(clk), .Q(d_ff_14_q));  // open: Qn, preset, reset
  xor xor_13 (r1_t, d_ff_13_q, in_1);
  xor xor_14 (r0, d_ff_14_q, in_1);

  // Other names for the same wires on the sheet: o0 = out_28; O1 = out_40; o1_t = out_27; O2 = out_39; o2_t = out_26;
  //   O3 = out_38; o3_t = out_25; O4 = out_37; op = in_1; ov = out_29

  // Notes on the sheet:
  //   add/sub command
  //   L input
  //   A-out output
  //   status output
endmodule
