// Logisim project project.circ as structural Verilog
module Instruction_RAM (
  input  clock,
  input  [2:0] address,
  input  mode,
  input  [3:0] data_in,
  output [3:0] data_out
);

  wire and_1_out, and_2_out, and_3_out, and_4_out, and_5_out, and_6_out, and_7_out, and_8_out, and_9_out,
       and_10_out, and_11_out, and_12_out, and_13_out, and_14_out, and_15_out, and_16_out, and_17_out,
       and_18_out, and_19_out, and_20_out, and_21_out, and_22_out, and_23_out, and_24_out, and_25_out,
       and_26_out, and_27_out, and_28_out, and_29_out, and_30_out, and_31_out, and_32_out, and_33_out,
       and_34_out, and_35_out, and_36_out, and_37_out, and_38_out, and_39_out, and_40_out, and_41_out,
       and_42_out, and_43_out, and_44_out, and_45_out, and_46_out, and_47_out, and_48_out, and_49_out,
       and_50_out, d_ff_1_q, d_ff_1_qn, d_ff_2_q, d_ff_2_qn, d_ff_3_q, d_ff_3_qn, d_ff_4_q, d_ff_4_qn,
       d_ff_5_q, d_ff_6_q, d_ff_7_q, d_ff_8_q, d_ff_9_q, d_ff_10_q, d_ff_11_q, d_ff_12_q, d_ff_13_q,
       d_ff_15_q, d_ff_16_q, d_ff_17_q, d_ff_18_q, d_ff_19_q, d_ff_20_q, d_ff_21_q, d_ff_22_q, d_ff_23_q,
       d_ff_25_q, d_ff_26_q, d_ff_27_q, d_ff_28_q, d_ff_29_q, d_ff_30_q, d_ff_31_q, d_ff_32_q, d_ff_33_q,
       d_ff_35_q, d_ff_36_q, d_ff_37_q, d_ff_38_q, d_ff_39_q, d_ff_40_q, d_ff_41_q, d_ff_42_q, d_ff_43_q,
       or_1_out, or_2_out, or_3_out, or_4_out;

  D_Flip_Flop d_ff_1 (.D(address[0]), .clk(clock), .Q(d_ff_1_q), .Qn(d_ff_1_qn));  // open: preset, reset
  D_Flip_Flop d_ff_2 (.D(address[1]), .clk(clock), .Q(d_ff_2_q), .Qn(d_ff_2_qn));  // open: preset, reset
  D_Flip_Flop d_ff_3 (.D(address[2]), .clk(clock), .Q(d_ff_3_q), .Qn(d_ff_3_qn));  // open: preset, reset
  D_Flip_Flop d_ff_4 (.D(mode), .clk(clock), .Q(d_ff_4_q), .Qn(d_ff_4_qn));  // open: preset, reset
  and and_1 (and_1_out, d_ff_1_q, d_ff_2_q, d_ff_3_q);
  and and_2 (and_2_out, d_ff_1_q, d_ff_2_q, d_ff_3_qn);
  and and_3 (and_3_out, d_ff_1_q, d_ff_2_qn, d_ff_3_q);
  and and_4 (and_4_out, d_ff_1_q, d_ff_2_qn, d_ff_3_qn);
  and and_5 (and_5_out, d_ff_1_qn, d_ff_2_q, d_ff_3_q);
  and and_6 (and_6_out, d_ff_1_qn, d_ff_2_q, d_ff_3_qn);
  and and_7 (and_7_out, d_ff_1_qn, d_ff_2_qn, d_ff_3_q);
  and and_8 (and_8_out, d_ff_1_qn, d_ff_2_qn, d_ff_3_qn);
  and and_9 (and_9_out, clock, d_ff_4_q);
  and and_10 (and_10_out, d_ff_4_qn, clock);
  D_Flip_Flop d_ff_5 (.D(d_ff_13_q), .clk(and_11_out), .Q(d_ff_5_q));  // open: Qn, preset, reset
  and and_11 (and_11_out, and_1_out, and_10_out);
  D_Flip_Flop d_ff_6 (.D(d_ff_13_q), .clk(and_12_out), .Q(d_ff_6_q));  // open: Qn, preset, reset
  and and_12 (and_12_out, and_2_out, and_10_out);
  D_Flip_Flop d_ff_7 (.D(d_ff_13_q), .clk(and_13_out), .Q(d_ff_7_q));  // open: Qn, preset, reset
  and and_13 (and_13_out, and_3_out, and_10_out);
  D_Flip_Flop d_ff_8 (.D(d_ff_13_q), .clk(and_14_out), .Q(d_ff_8_q));  // open: Qn, preset, reset
  and and_14 (and_14_out, and_4_out, and_10_out);
  D_Flip_Flop d_ff_9 (.D(d_ff_13_q), .clk(and_15_out), .Q(d_ff_9_q));  // open: Qn, preset, reset
  and and_15 (and_15_out, and_5_out, and_10_out);
  D_Flip_Flop d_ff_10 (.D(d_ff_13_q), .clk(and_16_out), .Q(d_ff_10_q));  // open: Qn, preset, reset
  and and_16 (and_16_out, and_6_out, and_10_out);
  D_Flip_Flop d_ff_11 (.D(d_ff_13_q), .clk(and_17_out), .Q(d_ff_11_q));  // open: Qn, preset, reset
  and and_17 (and_17_out, and_7_out, and_10_out);
  D_Flip_Flop d_ff_12 (.D(d_ff_13_q), .clk(and_18_out), .Q(d_ff_12_q));  // open: Qn, preset, reset
  and and_18 (and_18_out, and_8_out, and_10_out);
  D_Flip_Flop d_ff_13 (.D(data_in[3]), .clk(and_10_out), .Q(d_ff_13_q));  // open: Qn, preset, reset
  and and_19 (and_19_out, d_ff_5_q, and_1_out);
  and and_20 (and_20_out, d_ff_6_q, and_2_out);
  and and_21 (and_21_out, d_ff_7_q, and_3_out);
  and and_22 (and_22_out, d_ff_8_q, and_4_out);
  and and_23 (and_23_out, d_ff_9_q, and_5_out);
  and and_24 (and_24_out, d_ff_10_q, and_6_out);
  and and_25 (and_25_out, d_ff_11_q, and_7_out);
  and and_26 (and_26_out, d_ff_12_q, and_8_out);
  or or_1 (or_1_out, and_26_out, and_25_out, and_24_out, and_23_out, and_22_out, and_21_out, and_20_out, and_19_out);
  D_Flip_Flop d_ff_14 (.D(or_1_out), .clk(and_9_out), .Q(data_out[3]));  // open: Qn, preset, reset
  D_Flip_Flop d_ff_15 (.D(d_ff_23_q), .clk(and_11_out), .Q(d_ff_15_q));  // open: Qn, preset, reset
  D_Flip_Flop d_ff_16 (.D(d_ff_23_q), .clk(and_12_out), .Q(d_ff_16_q));  // open: Qn, preset, reset
  D_Flip_Flop d_ff_17 (.D(d_ff_23_q), .clk(and_13_out), .Q(d_ff_17_q));  // open: Qn, preset, reset
  D_Flip_Flop d_ff_18 (.D(d_ff_23_q), .clk(and_14_out), .Q(d_ff_18_q));  // open: Qn, preset, reset
  D_Flip_Flop d_ff_19 (.D(d_ff_23_q), .clk(and_15_out), .Q(d_ff_19_q));  // open: Qn, preset, reset
  D_Flip_Flop d_ff_20 (.D(d_ff_23_q), .clk(and_16_out), .Q(d_ff_20_q));  // open: Qn, preset, reset
  D_Flip_Flop d_ff_21 (.D(d_ff_23_q), .clk(and_17_out), .Q(d_ff_21_q));  // open: Qn, preset, reset
  D_Flip_Flop d_ff_22 (.D(d_ff_23_q), .clk(and_18_out), .Q(d_ff_22_q));  // open: Qn, preset, reset
  D_Flip_Flop d_ff_23 (.D(data_in[2]), .clk(and_10_out), .Q(d_ff_23_q));  // open: Qn, preset, reset
  and and_27 (and_27_out, d_ff_15_q, and_1_out);
  and and_28 (and_28_out, d_ff_16_q, and_2_out);
  and and_29 (and_29_out, d_ff_17_q, and_3_out);
  and and_30 (and_30_out, d_ff_18_q, and_4_out);
  and and_31 (and_31_out, d_ff_19_q, and_5_out);
  and and_32 (and_32_out, d_ff_20_q, and_6_out);
  and and_33 (and_33_out, d_ff_21_q, and_7_out);
  and and_34 (and_34_out, d_ff_22_q, and_8_out);
  D_Flip_Flop d_ff_24 (.D(or_2_out), .clk(and_9_out), .Q(data_out[2]));  // open: Qn, preset, reset
  D_Flip_Flop d_ff_25 (.D(d_ff_33_q), .clk(and_11_out), .Q(d_ff_25_q));  // open: Qn, preset, reset
  D_Flip_Flop d_ff_26 (.D(d_ff_33_q), .clk(and_12_out), .Q(d_ff_26_q));  // open: Qn, preset, reset
  D_Flip_Flop d_ff_27 (.D(d_ff_33_q), .clk(and_13_out), .Q(d_ff_27_q));  // open: Qn, preset, reset
  D_Flip_Flop d_ff_28 (.D(d_ff_33_q), .clk(and_14_out), .Q(d_ff_28_q));  // open: Qn, preset, reset
  D_Flip_Flop d_ff_29 (.D(d_ff_33_q), .clk(and_15_out), .Q(d_ff_29_q));  // open: Qn, preset, reset
  D_Flip_Flop d_ff_30 (.D(d_ff_33_q), .clk(and_16_out), .Q(d_ff_30_q));  // open: Qn, preset, reset
  D_Flip_Flop d_ff_31 (.D(d_ff_33_q), .clk(and_17_out), .Q(d_ff_31_q));  // open: Qn, preset, reset
  D_Flip_Flop d_ff_32 (.D(d_ff_33_q), .clk(and_18_out), .Q(d_ff_32_q));  // open: Qn, preset, reset
  or or_2 (or_2_out, and_34_out, and_33_out, and_32_out, and_31_out, and_30_out, and_29_out, and_28_out, and_27_out);
  D_Flip_Flop d_ff_33 (.D(data_in[1]), .clk(and_10_out), .Q(d_ff_33_q));  // open: Qn, preset, reset
  and and_35 (and_35_out, d_ff_25_q, and_1_out);
  and and_36 (and_36_out, d_ff_26_q, and_2_out);
  and and_37 (and_37_out, d_ff_27_q, and_3_out);
  and and_38 (and_38_out, d_ff_28_q, and_4_out);
  and and_39 (and_39_out, d_ff_29_q, and_5_out);
  and and_40 (and_40_out, d_ff_30_q, and_6_out);
  and and_41 (and_41_out, d_ff_31_q, and_7_out);
  and and_42 (and_42_out, d_ff_32_q, and_8_out);
  or or_3 (or_3_out, and_42_out, and_41_out, and_40_out, and_39_out, and_38_out, and_37_out, and_36_out, and_35_out);
  D_Flip_Flop d_ff_34 (.D(or_3_out), .clk(and_9_out), .Q(data_out[1]));  // open: Qn, preset, reset
  D_Flip_Flop d_ff_35 (.D(d_ff_43_q), .clk(and_11_out), .Q(d_ff_35_q));  // open: Qn, preset, reset
  D_Flip_Flop d_ff_36 (.D(d_ff_43_q), .clk(and_12_out), .Q(d_ff_36_q));  // open: Qn, preset, reset
  D_Flip_Flop d_ff_37 (.D(d_ff_43_q), .clk(and_13_out), .Q(d_ff_37_q));  // open: Qn, preset, reset
  D_Flip_Flop d_ff_38 (.D(d_ff_43_q), .clk(and_14_out), .Q(d_ff_38_q));  // open: Qn, preset, reset
  D_Flip_Flop d_ff_39 (.D(d_ff_43_q), .clk(and_15_out), .Q(d_ff_39_q));  // open: Qn, preset, reset
  D_Flip_Flop d_ff_40 (.D(d_ff_43_q), .clk(and_16_out), .Q(d_ff_40_q));  // open: Qn, preset, reset
  D_Flip_Flop d_ff_41 (.D(d_ff_43_q), .clk(and_17_out), .Q(d_ff_41_q));  // open: Qn, preset, reset
  D_Flip_Flop d_ff_42 (.D(d_ff_43_q), .clk(and_18_out), .Q(d_ff_42_q));  // open: Qn, preset, reset
  D_Flip_Flop d_ff_43 (.D(data_in[0]), .clk(and_10_out), .Q(d_ff_43_q));  // open: Qn, preset, reset
  and and_43 (and_43_out, d_ff_35_q, and_1_out);
  and and_44 (and_44_out, d_ff_36_q, and_2_out);
  and and_45 (and_45_out, d_ff_37_q, and_3_out);
  and and_46 (and_46_out, d_ff_38_q, and_4_out);
  and and_47 (and_47_out, d_ff_39_q, and_5_out);
  and and_48 (and_48_out, d_ff_40_q, and_6_out);
  and and_49 (and_49_out, d_ff_41_q, and_7_out);
  and and_50 (and_50_out, d_ff_42_q, and_8_out);
  D_Flip_Flop d_ff_44 (.D(or_4_out), .clk(and_9_out), .Q(data_out[0]));  // open: Qn, preset, reset
  or or_4 (or_4_out, and_50_out, and_49_out, and_48_out, and_47_out, and_46_out, and_45_out, and_44_out, and_43_out);

  // Notes on the sheet:
  //   mode: pull=up
endmodule

module IR (
  input  [3:0] instruction,
  input  clock
);

  wire add, halt, jump, load, op0, op1, ram, rgstr, save, sub, undriven;

  D_Flip_Flop d_ff_1 (.D(instruction[3]), .clk(clock), .Q(op1));  // open: Qn, preset, reset
  D_Flip_Flop d_ff_2 (.D(instruction[2]), .clk(clock), .Q(op0));  // open: Qn, preset, reset
  and and_1 (sub, op0, ~halt, op1);  // AND_Gate
  and and_2 (add, ~op0, op1);  // AND_Gate
  and and_3 (save, op0, ~op1);  // AND_Gate
  and and_4 (load, ~op0, ~jump, ~op1);  // AND_Gate
  and and_5 (halt, op0, op1, rgstr, ram);
  and and_6 (jump, ~op0, ~op1, ~rgstr, ~ram);  // AND_Gate
  D_Flip_Flop d_ff_3 (.D(instruction[1]), .clk(clock), .Q(rgstr));  // open: Qn, preset, reset
  D_Flip_Flop d_ff_4 (.D(instruction[0]), .clk(clock), .Q(ram));  // open: Qn, preset, reset
  D_Flip_Flop d_ff_5 (.clk(undriven));  // open: D, Q, Qn, preset, reset
  D_Flip_Flop d_ff_6 (.clk(undriven));  // open: D, Q, Qn, preset, reset
  D_Flip_Flop d_ff_7 ();  // open: D, clk, Q, Qn, preset, reset
  D_Flip_Flop d_ff_8 ();  // open: D, clk, Q, Qn, preset, reset
  D_Flip_Flop d_ff_9 ();  // open: D, clk, Q, Qn, preset, reset
  D_Flip_Flop d_ff_10 ();  // open: D, clk, Q, Qn, preset, reset
  D_Flip_Flop d_ff_11 ();  // open: D, clk, Q, Qn, preset, reset
  D_Flip_Flop d_ff_12 ();  // open: D, clk, Q, Qn, preset, reset
  D_Flip_Flop d_ff_13 ();  // open: D, clk, Q, Qn, preset, reset
  D_Flip_Flop d_ff_14 ();  // open: D, clk, Q, Qn, preset, reset
  D_Flip_Flop d_ff_15 ();  // open: D, clk, Q, Qn, preset, reset
  D_Flip_Flop d_ff_16 ();  // open: D, clk, Q, Qn, preset, reset
  D_Flip_Flop d_ff_17 ();  // open: D, clk, Q, Qn, preset, reset
  D_Flip_Flop d_ff_18 ();  // open: D, clk, Q, Qn, preset, reset
  D_Flip_Flop d_ff_19 ();  // open: D, clk, Q, Qn, preset, reset
  D_Flip_Flop d_ff_20 ();  // open: D, clk, Q, Qn, preset, reset
  D_Flip_Flop d_ff_21 ();  // open: D, clk, Q, Qn, preset, reset
  D_Flip_Flop d_ff_22 ();  // open: D, clk, Q, Qn, preset, reset
  D_Flip_Flop d_ff_23 ();  // open: D, clk, Q, Qn, preset, reset
  D_Flip_Flop d_ff_24 ();  // open: D, clk, Q, Qn, preset, reset

  // Other names for the same wires on the sheet: clk = clock

  // Notes on the sheet:
  //   sub
  //   add
  //   save
  //   load
  //   halt
  //   jump
endmodule

module ALU (
  input  in_1,
  input  in_2,
  input  in_3,
  input  in_4,
  input  in_5,
  input  in_6,
  input  in_7,
  input  in_8,
  input  in_9,
  output out_10,
  output out_11,
  output out_12,
  output out_13,
  output out_14,
  output out_15,
  output out_16
);

  wire and_1_out, and_2_out, and_3_out, and_4_out, and_5_out, and_6_out, and_7_out, and_8_out, and_9_out,
       and_10_out, and_11_out, and_12_out, C1, C2, C3, C4, clk, L1, L2, L3, L4, not_1_out, not_2_out,
       not_3_out, not_4_out, not_5_out, O1, O2, O3, O4, OP, or_1_out, or_3_out, or_5_out, or_7_out, R1, r1_t,
       R2, r2_t, R3, r3_t, R4, r4_t, xor_1_out, xor_3_out, xor_5_out, xor_7_out;

  D_Flip_Flop d_ff_1 (.D(in_1), .clk(clk), .Q(OP));  // open: Qn, preset, reset
  D_Flip_Flop d_ff_2 (.D(in_2), .clk(clk), .Q(L4));  // open: Qn, preset, reset
  and and_1 (and_1_out, L4, R4);
  and and_2 (and_2_out, L4, C3);
  or or_1 (or_1_out, and_1_out, and_2_out);
  or or_2 (C4, or_1_out, and_3_out);
  xor xor_1 (xor_1_out, L4, R4);
  D_Flip_Flop d_ff_3 (.D(in_3), .clk(clk), .Q(L3));  // open: Qn, preset, reset
  and and_3 (and_3_out, R4, C3);
  and and_4 (and_4_out, L3, R3);
  or or_3 (or_3_out, and_4_out, and_5_out);
  xor xor_2 (O4, xor_1_out, C3);
  D_Flip_Flop d_ff_4 (.D(O4), .clk(clk), .Q(out_10));  // open: Qn, preset, reset
  D_Flip_Flop d_ff_5 (.D(in_4), .clk(clk), .Q(L2));  // open: Qn, preset, reset
  and and_5 (and_5_out, L3, C2);
  and and_6 (and_6_out, R3, C2);
  or or_4 (C3, or_3_out, and_6_out);
  xor xor_3 (xor_3_out, L3, R3);
  xor xor_4 (O3, xor_3_out, C2);
  D_Flip_Flop d_ff_6 (.D(O3), .clk(clk), .Q(out_11));  // open: Qn, preset, reset
  D_Flip_Flop d_ff_7 (.D(in_5), .clk(clk), .Q(L1));  // open: Qn, preset, reset
  D_Flip_Flop d_ff_8 (.D(in_6), .clk(clk), .Q(r4_t));  // open: Qn, preset, reset
  and and_7 (and_7_out, L2, R2);
  and and_8 (and_8_out, L2, C1);
  or or_5 (or_5_out, and_7_out, and_8_out);
  or or_6 (C2, or_5_out, and_9_out);
  D_Flip_Flop d_ff_9 (.D(O2), .clk(clk), .Q(out_12));  // open: Qn, preset, reset
  D_Flip_Flop d_ff_10 (.D(in_7), .clk(clk), .Q(r3_t));  // open: Qn, preset, reset
  and and_9 (and_9_out, R2, C1);
  and and_10 (and_10_out, L1, R1);
  xor xor_5 (xor_5_out, L2, R2);
  xor xor_6 (O2, xor_5_out, C1);
  D_Flip_Flop d_ff_11 (.D(O1), .clk(clk), .Q(out_13));  // open: Qn, preset, reset
  D_Flip_Flop d_ff_12 (.D(in_8), .clk(clk), .Q(r2_t));  // open: Qn, preset, reset
  and and_11 (and_11_out, L1, OP);
  and and_12 (and_12_out, R1, OP);
  or or_7 (or_7_out, and_10_out, and_11_out);
  or or_8 (C1, or_7_out, and_12_out);
  xor xor_7 (xor_7_out, L1, R1);
  xor xor_8 (O1, xor_7_out, OP);
  D_Flip_Flop d_ff_13 (.D(in_9), .clk(clk), .Q(r1_t));  // open: Qn, preset, reset
  xor xor_9 (R4, OP, r4_t);
  xor xor_10 (R3, OP, r3_t);
  xor xor_11 (out_14, C4, C3);
  not not_1 (not_1_out, out_14);
  and and_13 (out_16, O4, not_1_out);
  xor xor_12 (R2, OP, r2_t);
  xor xor_13 (R1, OP, r1_t);
  not not_2 (not_2_out, O4);
  not not_3 (not_3_out, O3);
  not not_4 (not_4_out, O2);
  not not_5 (not_5_out, O1);
  and and_14 (out_15, not_2_out, not_3_out, not_4_out, not_5_out);

  // Other names for the same wires on the sheet: neg = out_16; over = out_14; zero = out_15

  // Notes on the sheet:
  //   carry out
  //   Mode
  //   4 carry
  //   4 out
  //   L Input
  //   3 carry
  //   3 out
  //   A Out
  //   2 carry
  //   status
  //   R Input
  //   2 out
  //   1 carry
  //   1 out
  //   carry in
  //   input
  //   complement
  //   status
  //   output
endmodule

module Data_RAM (
  input  in_1,
  input  in_2,
  input  in_3,
  input  in_4,
  input  in_5,
  input  in_6,
  output out_7,
  output out_8,
  output out_9,
  output out_10
);

  wire and_5_out, and_6_out, and_7_out, and_8_out, and_9_out, and_10_out, and_11_out, and_12_out,
       clock_1_out, d_ff_1_q, d_ff_2_q, d_ff_3_q, d_ff_5_q, d_ff_6_q, d_ff_7_q, d_ff_9_q, d_ff_10_q,
       d_ff_11_q, d_ff_13_q, d_ff_14_q, d_ff_15_q, load, or_1_out, or_2_out, or_3_out, or_4_out, save, save0,
       save1;

  Clock clock_1 (.out(clock_1_out));
  and and_1 (save, ~in_2, clock_1_out);  // AND_Gate
  and and_2 (load, clock_1_out, in_2);
  and and_3 (save1, save, in_1);
  and and_4 (save0, save, ~in_1);  // AND_Gate
  D_Flip_Flop d_ff_1 (.D(in_3), .clk(save), .Q(d_ff_1_q));  // open: Qn, preset, reset
  D_Flip_Flop d_ff_2 (.D(d_ff_1_q), .clk(save1), .Q(d_ff_2_q));  // open: Qn, preset, reset
  and and_5 (and_5_out, d_ff_2_q, in_1);
  D_Flip_Flop d_ff_3 (.D(d_ff_1_q), .clk(save0), .Q(d_ff_3_q));  // open: Qn, preset, reset
  or or_1 (or_1_out, and_6_out, and_5_out);
  D_Flip_Flop d_ff_4 (.D(or_1_out), .clk(load), .Q(out_7));  // open: Qn, preset, reset
  and and_6 (and_6_out, d_ff_3_q, ~in_1);  // AND_Gate
  D_Flip_Flop d_ff_5 (.D(d_ff_7_q), .clk(save1), .Q(d_ff_5_q));  // open: Qn, preset, reset
  D_Flip_Flop d_ff_6 (.D(d_ff_7_q), .clk(save0), .Q(d_ff_6_q));  // open: Qn, preset, reset
  D_Flip_Flop d_ff_7 (.D(in_4), .clk(save), .Q(d_ff_7_q));  // open: Qn, preset, reset
  D_Flip_Flop d_ff_8 (.D(or_2_out), .clk(load), .Q(out_8));  // open: Qn, preset, reset
  and and_7 (and_7_out, d_ff_5_q, in_1);
  and and_8 (and_8_out, d_ff_6_q, ~in_1);  // AND_Gate
  or or_2 (or_2_out, and_8_out, and_7_out);
  D_Flip_Flop d_ff_9 (.D(d_ff_11_q), .clk(save1), .Q(d_ff_9_q));  // open: Qn, preset, reset
  D_Flip_Flop d_ff_10 (.D(d_ff_11_q), .clk(save0), .Q(d_ff_10_q));  // open: Qn, preset, reset
  D_Flip_Flop d_ff_11 (.D(in_5), .clk(save), .Q(d_ff_11_q));  // open: Qn, preset, reset
  and and_9 (and_9_out, d_ff_9_q, in_1);
  and and_10 (and_10_out, d_ff_10_q, ~in_1);  // AND_Gate
  or or_3 (or_3_out, and_10_out, and_9_out);
  D_Flip_Flop d_ff_12 (.D(or_3_out), .clk(load), .Q(out_9));  // open: Qn, preset, reset
  D_Flip_Flop d_ff_13 (.D(d_ff_15_q), .clk(save1), .Q(d_ff_13_q));  // open: Qn, preset, reset
  D_Flip_Flop d_ff_14 (.D(d_ff_15_q), .clk(save0), .Q(d_ff_14_q));  // open: Qn, preset, reset
  D_Flip_Flop d_ff_15 (.D(in_6), .clk(save), .Q(d_ff_15_q));  // open: Qn, preset, reset
  and and_11 (and_11_out, d_ff_13_q, in_1);
  and and_12 (and_12_out, d_ff_14_q, ~in_1);  // AND_Gate
  or or_4 (or_4_out, and_12_out, and_11_out);
  D_Flip_Flop d_ff_16 (.D(or_4_out), .clk(load), .Q(out_10));  // open: Qn, preset, reset

  // Other names for the same wires on the sheet: adrs = in_1; in1 = in_3; in2 = in_4; in3 = in_5; in4 = in_6;
  //   mode = in_2; o1 = out_7; o2 = out_8; o3 = out_9; o4 = out_10

  // Notes on the sheet:
  //   ADDRESS
  //   MODE
  //   INPUT
  //   OUTPUT
endmodule

module main (
  input  [2:0] in_1,
  input  in_2,
  input  [3:0] in_3
);

  wire clk;
  wire [3:0] instruction_ram_1_data_out;

  Clock clock_1 (.out(clk));
  // Probe on instruction_ram_1_data_out
  Instruction_RAM instruction_ram_1 (
    .clock(clk), .address(in_1), .mode(in_2), .data_in(in_3), .data_out(instruction_ram_1_data_out));
  IR ir_1 (.instruction(instruction_ram_1_data_out));  // open: clock
endmodule
