// Logisim project project_template.circ as structural Verilog: 7 circuits, main circuit main
module main (
  input  in_1,
  input  in_2,
  input  in_3,
  input  in_4,
  input  in_5,
  input  in_6,
  input  in_7,
  input  in_8,
  input  [1:0] in_9
);

  wire ALUOp, ALUSrc, Branch, MemRead, MemtoReg, MemWrite, multiplexer_1_out, RegDst, RegWrite;
  wire [2:0] add_1_new_adr, pc_1_cur_adr;
  wire [3:0] instruction_ram_1_instruction, multiplexer_2_out, register_block_1_read_d1,
       register_block_1_read_d2, undriven;

  pc pc_1 (.next_adr(add_1_new_adr), .cur_adr(pc_1_cur_adr));
  // Probe on pc_1_cur_adr
  control control_1 (
    .RegDst(RegDst), .Branch(Branch), .MemRead(MemRead), .MemtoReg(MemtoReg), .ALUOp(ALUOp),
    .MemWrite(MemWrite), .ALUSrc(ALUSrc), .RegWrite(RegWrite));  // open: in_1
  add add_1 (.old_adr(pc_1_cur_adr), .increment(in_9), .new_adr(add_1_new_adr));
  instruction_ram instruction_ram_1 (.read_adr(pc_1_cur_adr), .instruction(instruction_ram_1_instruction));
  Multiplexer multiplexer_1 (
    .in0(instruction_ram_1_instruction[1]), .in1(instruction_ram_1_instruction[2]), .out(multiplexer_1_out),
    .sel(RegDst));
  register_block register_block_1 (
    .read_r1(instruction_ram_1_instruction[0]), .read_r2(instruction_ram_1_instruction[1]),
    .write_r(multiplexer_1_out), .write_d(undriven), .read_d1(register_block_1_read_d1),
    .read_d2(register_block_1_read_d2));
  Multiplexer #(.width(4)) multiplexer_2 (.in0(register_block_1_read_d2), .out(multiplexer_2_out));  // open: in1, sel
  alu alu_1 (.operation(ALUOp), .R_in(multiplexer_2_out), .L_in(register_block_1_read_d1));  // open: status
endmodule

module add (
  input  [2:0] old_adr,
  input  [1:0] increment,
  output [2:0] new_adr
);
endmodule

module pc (
  input  [2:0] next_adr,
  output [2:0] cur_adr
);
endmodule

module instruction_ram (
  input  [2:0] read_adr,
  output [3:0] instruction
);
endmodule

module register_block (
  input  read_r1,
  input  read_r2,
  input  write_r,
  input  [3:0] write_d,
  output [3:0] read_d1,
  output [3:0] read_d2
);
endmodule

module alu (
  input  operation,
  input  [3:0] R_in,
  input  [3:0] L_in,
  output [2:0] status
);
endmodule

module control (
  input  in_1,
  output RegDst,
  output Branch,
  output MemRead,
  output MemtoReg,
  output ALUOp,
  output MemWrite,
  output ALUSrc,
  output RegWrite
);
endmodule
