// Logisim project t2.circ as structural Verilog: 1 circuit, main circuit main
module main (
  input  in_1,
  input  a_b_4,
  input  in_3,
  input  in_4,
  input  in_5,
  input  in_6,
  input  in_7,
  input  a_b_1,
  input  in_9,
  output out_10,
  output out_11,
  output out_12,
  output out_13,
  output out_14,
  output out_15,
  output out_16
);

  wire and_1_out, and_2_out, and_3_out, and_4_out, and_5_out, and_6_out, and_7_out, and_8_out, and_10_out,
       and_11_out, and_12_out, and_13_out, and_14_out, and_15_out, and_16_out, b1, b2, b3, b4, c1, c2, c3,
       or_1_out, or_3_out, or_5_out, or_7_out, xor_1_out, xor_3_out, xor_5_out, xor_9_out, xor_12_out;

  and and_1 (and_1_out, in_1, b4);
  or or_1 (or_1_out, and_1_out, and_2_out);
  xor xor_1 (xor_1_out, in_1, b4);
  xor xor_2 (out_13, xor_1_out, c3);
  and and_2 (and_2_out, in_1, c3);
  or or_2 (out_10, or_1_out, and_3_out);
  and and_3 (and_3_out, b4, c3);
  and and_4 (and_4_out, in_3, b3);
  and and_5 (and_5_out, out_13, out_14);
  and and_6 (and_6_out, out_15, out_16);
  and and_7 (and_7_out, and_5_out, and_6_out);
  not not_1 (out_11, and_7_out);
  xor xor_3 (xor_3_out, in_3, b3);
  xor xor_4 (out_14, xor_3_out, c2);
  and and_8 (and_8_out, in_3, c2);
  or or_3 (or_3_out, and_4_out, and_8_out);
  or or_4 (c3, or_3_out, and_10_out);
  xor xor_5 (xor_5_out, out_13, in_1);
  and and_9 (out_12, and_7_out, xor_5_out);
  xor xor_6 (b4, in_9, a_b_4);
  xor xor_7 (b3, in_9, in_4);
  and and_10 (and_10_out, b3, c2);
  xor xor_8 (b2, in_9, in_6);
  xor xor_9 (xor_9_out, in_5, b2);
  xor xor_10 (out_15, xor_9_out, c1);
  and and_11 (and_11_out, in_5, b2);
  and and_12 (and_12_out, in_5, c1);
  or or_5 (or_5_out, and_11_out, and_12_out);
  or or_6 (c2, or_5_out, and_13_out);
  xor xor_11 (b1, in_9, a_b_1);
  and and_13 (and_13_out, b2, c1);
  and and_14 (and_14_out, in_7, b1);
  xor xor_12 (xor_12_out, in_7, b1);
  xor xor_13 (out_16, xor_12_out, in_9);
  and and_15 (and_15_out, in_7, in_9);
  or or_7 (or_7_out, and_14_out, and_15_out);
  or or_8 (c1, or_7_out, and_16_out);
  and and_16 (and_16_out, b1, in_9);

  // Other names for the same wires on the sheet: a1 = in_7; a2 = in_5; a3 = in_3; a4 = in_1; neg = out_12;
  //   o1 = out_16; o2 = out_15; o3 = out_14; o4 = out_13; op = in_9; ov = out_10; zero = out_11

  // Notes on the sheet:
  //   4 out
  //   4 carry
  //   3 out
  //   3 carry
  //   a b 3
  //   a b 2
  //   2 out
  //   2 carry
  //   op
  //   1 out
  //   1 carry
  //   carry in
endmodule
