// Logisim project tmp.circ as structural Verilog: 1 circuit, main circuit main
module main (
  input  in_1,
  input  in_2,
  input  in_3,
  input  in_4,
  input  in_5,
  input  in_6,
  input  in_7,
  input  in_8,
  input  in_9,
  output out_10,
  output out_11,
  output out_12,
  output out_13,
  output out_14,
  output out_15
);

  wire and_1_out, and_4_out, and_5_out, and_6_out, and_7_out, and_8_out, and_9_out, and_10_out, and_11_out,
       and_12_out, and_13_out, and_14_out, c0, c1, c2, clk, l0, l1, l2, l3, or_1_out, r0, r1, r2, r3,
       xor_1_out, xor_2_out, xor_4_out, xor_6_out, xor_8_out;

  Clock clock_1 (.out(clk));
  and and_1 (and_1_out, l3, xor_2_out);
  and and_2 (out_14, in_9, xor_1_out);
  xor xor_1 (xor_1_out, or_1_out, in_9);
  and and_3 (out_15, xor_1_out, ~in_9);  // AND_Gate
  xor xor_2 (xor_2_out, r3, in_9);
  and and_4 (and_4_out, l3, c2);
  and and_5 (and_5_out, xor_2_out, c2);
  or or_1 (or_1_out, and_1_out, and_4_out, and_5_out);
  D_Flip_Flop d_ff_1 (.D(in_1), .clk(clk), .Q(r3));  // open: Qn, preset, reset
  D_Flip_Flop d_ff_2 (.D(in_5), .clk(clk), .Q(l3));  // open: Qn, preset, reset
  and and_6 (and_6_out, l2, xor_4_out);
  xor xor_3 (out_10, c2, xor_2_out, l3);
  D_Flip_Flop d_ff_3 (.D(in_2), .clk(clk), .Q(r2));  // open: Qn, preset, reset
  D_Flip_Flop d_ff_4 (.D(in_6), .clk(clk), .Q(l2));  // open: Qn, preset, reset
  xor xor_4 (xor_4_out, r2, in_9);
  and and_7 (and_7_out, l2, c1);
  and and_8 (and_8_out, xor_4_out, c1);
  xor xor_5 (out_11, c1, xor_4_out, l2);
  or or_2 (c2, and_6_out, and_7_out, and_8_out);
  D_Flip_Flop d_ff_5 (.D(in_3), .clk(clk), .Q(r1));  // open: Qn, preset, reset
  D_Flip_Flop d_ff_6 (.D(in_7), .clk(clk), .Q(l1));  // open: Qn, preset, reset
  and and_9 (and_9_out, l1, xor_6_out);
  and and_10 (and_10_out, l1, c0);
  or or_3 (c1, and_9_out, and_10_out, and_11_out);
  D_Flip_Flop d_ff_7 (.D(in_4), .clk(clk), .Q(r0));  // open: Qn, preset, reset
  D_Flip_Flop d_ff_8 (.D(in_8), .clk(clk), .Q(l0));  // open: Qn, preset, reset
  xor xor_6 (xor_6_out, r1, in_9);
  and and_11 (and_11_out, xor_6_out, c0);
  xor xor_7 (out_12, c0, xor_6_out, l1);
  xor xor_8 (xor_8_out, r0, in_9);
  and and_12 (and_12_out, l0, xor_8_out);
  and and_13 (and_13_out, l0, in_9);
  and and_14 (and_14_out, xor_8_out, in_9);
  or or_4 (c0, and_12_out, and_13_out, and_14_out);
  xor xor_9 (out_13, in_9, xor_8_out, l0);

  // Other names for the same wires on the sheet: neg = out_14; o0 = out_13; o1 = out_12; o2 = out_11; o3 = out_10;
  //   op = in_9; ov = out_15
endmodule
